# Fritzing sketch Vloerverwarming monitor (saved by Fritzing 0.9.3b)
breadboards: 1

parts:
  Raspberry_Pi_1 = Raspberry Pi 3 [part_number=RPI-3-V1.2]
  R3 = Resistor [tolerance=±5% resistance=3.3k package=THT]
  DS1 = DS18B20 1-Wire Temperature Sensor [part_number=DS18B20]
  DS2 = DS18B20 1-Wire Temperature Sensor [part_number=DS18B20]
  DS3 = DS18B20 1-Wire Temperature Sensor [part_number=DS18B20]
  DS4 = DS18B20 1-Wire Temperature Sensor [part_number=DS18B20]
  DS5 = DS18B20 1-Wire Temperature Sensor [part_number=DS18B20]
  DS6 = DS18B20 1-Wire Temperature Sensor [part_number=DS18B20]
  DS7 = DS18B20 1-Wire Temperature Sensor [part_number=DS18B20]
  DS8 = DS18B20 1-Wire Temperature Sensor [part_number=DS18B20]
  DS9 = DS18B20 1-Wire Temperature Sensor [part_number=DS18B20]
  DS10 = DS18B20 1-Wire Temperature Sensor [part_number=DS18B20]

nets:
  VDD: Raspberry_Pi_1.3v3, Raspberry_Pi_1.3V3, R3.Pin_0, DS1.VDD, DS2.VDD, DS3.VDD, DS4.VDD, DS5.VDD, DS6.VDD, DS7.VDD, DS8.VDD, DS9.VDD, DS10.VDD
  N1: Raspberry_Pi_1.GPIO4, R3.Pin_1, DS1.DQ, DS2.DQ, DS3.DQ, DS4.DQ, DS5.DQ, DS6.DQ, DS7.DQ, DS8.DQ, DS9.DQ, DS10.DQ
  GND: Raspberry_Pi_1.GND, DS1.GND, DS2.GND, DS3.GND, DS4.GND, DS5.GND, DS6.GND, DS7.GND, DS8.GND, DS9.GND, DS10.GND
